// Logisim project part1.circ as structural Verilog
module NAND1 (
  input  in_1,
  input  in_2,
  output out_3
);


  // Other names for the same wires on the sheet: Result = out_3; X = in_1; Y = in_2

  // Notes on the sheet:
  //   ------------------------------------------ Put your circuit below this line ------------------
endmodule

module NOR1 (
  input  in_1,
  input  in_2,
  output out_3
);


  // Other names for the same wires on the sheet: Result = out_3; X = in_1; Y = in_2

  // Notes on the sheet:
  //   ------------------------------------------ Put your circuit below this line ------------------
endmodule

module XOR1 (
  input  in_1,
  input  in_2,
  output out_3
);


  // Other names for the same wires on the sheet: Result = out_3; X = in_1; Y = in_2

  // Notes on the sheet:
  //   ------------------------------------------ Put your circuit below this line ------------------
endmodule

module Mux2to1 (
  input  in_1,
  input  in_2,
  input  in_3,
  output out_4
);


  // Other names for the same wires on the sheet: Result = out_4; S = in_3; X = in_1; Y = in_2

  // Notes on the sheet:
  //   ------------------------------------------ Put your circuit below this line ------------------
endmodule

module Dec2to4 (
  input  [1:0] in_1,
  output [3:0] out_2
);


  // Other names for the same wires on the sheet: Result[3:0] = out_2; S[1:0] = in_1

  // Notes on the sheet:
  //   S is decoder's 2-bit inputs
  //   ------------------------------------------ Put your circuit below this line ------------------
  //   Result is decoder's 4-bit outputs
endmodule

module Mux4to1 (
  input  in_1,
  input  in_2,
  input  in_3,
  input  in_4,
  input  [1:0] in_5,
  output out_6
);


  // Other names for the same wires on the sheet: A = in_1; B = in_2; C = in_3; D = in_4; Result = out_6;
  //   S[1:0] = in_5

  // Notes on the sheet:
  //   S=00 selects A
  //   S=01 selects B
  //   S=10 selects C
  //   S=11 selects D
  //   ------------------------------------------ Put your circuit below this line ------------------
endmodule

module NegSign (
  input  [7:0] in_1,
  output [7:0] out_2
);


  // Other names for the same wires on the sheet: Result[7:0] = out_2; X[7:0] = in_1

  // Notes on the sheet:
  //   ------------------------------------------ Put your circuit below this line ------------------
endmodule
